// Digital circuit cmd.dig as structural Verilog
module cmd (
  input  [5:0] Co,
  input  [5:0] Nf,
  input  [4:0] nrt,
  output ld,
  output str,
  output mx1,
  output bne,
  output beq,
  output blez,
  output bgtz,
  output jal,
  output jr,
  output Ns,
  output [4:0] Op,
  output ereg,
  output shamt,
  output M8,
  output \break ,
  output bltz,
  output bgez,
  output cns
);

  wire addi, addiu, \and , andi, Co1, comparator_1_eq, comparator_2_eq, div, divu, lb, lui, lw, mfhi, mflo,
       mult, multu, \nor , Op1, Op2, Op4, Op5, Op6, Op7, Op8, Op12, Op13, Op14, \or , ori, reg3, sb, sll,
       sllv, slt, slti, sltiu, sltu, sra, srav, srl, srlv, sub, subu, sw, \xor , xori;

  // decodeur64 decodeur64_1: pin names not known; wires that end beside it: Co, 1'b1, reg3, Co1, jal, beq, bne, blez, bgtz, addi, addiu, slti, sltiu, andi, ori, xori, lui
  // decodeur64 decodeur64_2: pin names not known; wires that end beside it: Nf, reg3, sll, srl, sra, sllv, srlv, srav, jr, \break , mfhi, mflo, mult, multu, div, divu
  or or_1 (mx1, reg3, beq, bne);
  or or_2 (str, sb, sw);
  or or_3 (ld, lb, lw, cns);
  or or_4 (Ns, andi, ori, xori);
  or or_5 (shamt, sll, srl, sra);
  or or_6 (M8, lb, cns, sb);
  nor nor_1 (ereg, bne, beq, \break , sb, sw, jr, mult, multu, div, divu, bltz, bgez, blez, bgtz);
  or or_7 (Op1, andi, \and );
  or or_8 (Op2, ori, \or );
  or or_9 (Op4, xori, \xor );
  or or_10 (Op5, sll, sllv);
  or or_11 (Op6, srl, srlv);
  or or_12 (Op7, sra, srav);
  or or_13 (Op8, bne, sub, beq, subu);
  or or_14 (Op12, slti, slt);
  or or_15 (Op13, sltu, sltiu);
  or or_16 (Op14, bltz, bgez, blez, bgtz);
  Comparator #(.Bits(5)) comparator_1 (.a(nrt), .b({5{1'b0}}), .eq(comparator_1_eq));  // open: gt, lt
  Comparator #(.Bits(5)) comparator_2 (.a(nrt), .b(5'b00001), .eq(comparator_2_eq));  // open: gt, lt
  encodeur32 encodeur32_1 (
    ._0(1'b0), ._1(Op1), ._2(Op2), ._3(\nor ), ._4(Op4), ._5(Op5), ._6(Op6), ._7(Op7), ._8(Op8), ._9(lui),
    ._10(mfhi), ._11(mflo), ._12(Op12), ._13(Op13), ._14(Op14), ._15(mult), ._16(multu), ._17(div),
    ._18(divu), ._19(1'b0), ._20(1'b0), ._21(1'b0), ._22(1'b0), ._23(1'b0), ._24(1'b0), ._25(1'b0),
    ._26(1'b0), ._27(1'b0), ._28(1'b0), ._29(1'b0), ._30(1'b0), ._31(1'b0), .s(Op));
  and and_1 (bltz, comparator_1_eq, Co1);
  and and_2 (bgez, comparator_2_eq, Co1);

  // Other names for the same wires on the sheet: Op17 = div; Op18 = divu; lbu = cns; Op9 = lui; Op10 = mfhi;
  //   Op11 = mflo; Op15 = mult; Op16 = multu; Op3 = \nor ; num_rt[4:0] = nrt

  // Notes on the sheet:
  //   Decodage Co et Nf
  //   Signaux du processeur
  //   Commande UAL
endmodule

/* Test case:
Co	Nf	nrt	Op	mx1	str	ld	bne	beq	Ns	shamt	ereg	break	M8	blez
0	0	0	5	1	0	0	0	0	0	1	1	0	0	0
0	2	0	6	1	0	0	0	0	0	1	1	0	0	0
0	3	0	7	1	0	0	0	0	0	1	1	0	0	0
0	4	0	5	1	0	0	0	0	0	0	1	0	0	0
0	6	0	6	1	0	0	0	0	0	0	1	0	0	0
0	7	0	7	1	0	0	0	0	0	0	1	0	0	0
0	8	0	x	1	0	0	0	0	0	0	0	0	0	0
0	13	0	x	1	0	0	0	0	0	0	0	1	0	0
0	16	0	10	1	0	0	0	0	0	0	1	0	0	0
0	18	0	11	1	0	0	0	0	0	0	1	0	0	0
0	24	0	15	1	0	0	0	0	0	0	0	0	0	0
0	25	0	16	1	0	0	0	0	0	0	0	0	0	0
0	26	0	17	1	0	0	0	0	0	0	0	0	0	0
0	27	0	18	1	0	0	0	0	0	0	0	0	0	0
0	32	0	0	1	0	0	0	0	0	0	1	0	0	0
0	33	0	0	1	0	0	0	0	0	0	1	0	0	0
0	34	0	8	1	0	0	0	0	0	0	1	0	0	0
0	35	0	8	1	0	0	0	0	0	0	1	0	0	0
0	36	0	1	1	0	0	0	0	0	0	1	0	0	0
0	37	0	2	1	0	0	0	0	0	0	1	0	0	0
0	38	0	4	1	0	0	0	0	0	0	1	0	0	0
0	39	0	3	1	0	0	0	0	0	0	1	0	0	0
0	42	0	12	1	0	0	0	0	0	0	1	0	0	0
0	43	0	13	1	0	0	0	0	0	0	1	0	0	0
1	0	0	14	0	0	0	0	0	0	0	0	0	0	0
1	0	1	14	0	0	0	0	0	0	0	0	0	0	0
3	0	0	x	0	0	0	0	0	0	0	1	0	0	0
4	0	0	8	1	0	0	0	1	0	0	0	0	0	0
5	0	0	8	1	0	0	1	0	0	0	0	0	0	0
6	0	0	14	0	0	0	0	0	0	0	0	0	0	1
7	0	0	14	0	0	0	0	0	0	0	0	0	0	0
8	0	0	0	0	0	0	0	0	0	0	1	0	0	0
9	0	0	0	0	0	0	0	0	0	0	1	0	0	0
10	0	0	12	0	0	0	0	0	0	0	1	0	0	0
11	0	0	13	0	0	0	0	0	0	0	1	0	0	0
12	0	0	1	0	0	0	0	0	1	0	1	0	0	0
13	0	0	2	0	0	0	0	0	1	0	1	0	0	0
14	0	0	4	0	0	0	0	0	1	0	1	0	0	0
15	0	0	9	0	0	0	0	0	0	0	1	0	0	0
32	0	0	0	0	0	1	0	0	0	0	1	0	1	0
35	0	0	0	0	0	1	0	0	0	0	1	0	0	0
36	0	0	0	0	0	1	0	0	0	0	1	0	1	0
40	0	0	0	0	1	0	0	0	0	0	0	0	1	0
43	0	0	0	0	1	0	0	0	0	0	0	0	0	0
*/
