// Digital circuit decodeur64.dig as structural Verilog
module decodeur64 (
  input  [5:0] e,
  input  en,
  output _0,
  output _1,
  output _2,
  output _3,
  output _4,
  output _5,
  output _6,
  output _7,
  output _8,
  output _9,
  output _10,
  output _11,
  output _12,
  output _13,
  output _14,
  output _15,
  output _16,
  output _17,
  output _18,
  output _19,
  output _20,
  output _21,
  output _22,
  output _23,
  output _24,
  output _25,
  output _26,
  output _27,
  output _28,
  output _29,
  output _30,
  output _31,
  output _32,
  output _33,
  output _34,
  output _35,
  output _36,
  output _37,
  output _38,
  output _39,
  output _40,
  output _41,
  output _42,
  output _43,
  output _44,
  output _45,
  output _46,
  output _47,
  output _48,
  output _49,
  output _50,
  output _51,
  output _52,
  output _53,
  output _54,
  output _55,
  output _56,
  output _57,
  output _58,
  output _59,
  output _60,
  output _61,
  output _62,
  output _63
);

  wire [63:0] bitextender_1_out, decoder_1_out_0;

  BitExtender #(.inputBits(1), .outputBits(64)) bitextender_1 (.in(en), .out(bitextender_1_out));
  assign {_63, _62, _61, _60, _59, _58, _57, _56, _55, _54, _53, _52, _51, _50, _49, _48, _47, _46, _45, _44, _43, _42, _41, _40, _39, _38, _37, _36, _35, _34, _33, _32, _31, _30, _29, _28, _27, _26, _25, _24, _23, _22, _21, _20, _19, _18, _17, _16, _15, _14, _13, _12, _11, _10, _9, _8, _7, _6, _5, _4, _3, _2, _1, _0} = decoder_1_out_0 & bitextender_1_out;  // And and_1, 64 bits wide
  Decoder #(.Selector_Bits(6)) decoder_1 (
    .sel(e), .out_0(decoder_1_out_0[0]), .out_1(decoder_1_out_0[1]), .out_2(decoder_1_out_0[2]),
    .out_3(decoder_1_out_0[3]), .out_4(decoder_1_out_0[4]), .out_5(decoder_1_out_0[5]),
    .out_6(decoder_1_out_0[6]), .out_7(decoder_1_out_0[7]), .out_8(decoder_1_out_0[8]),
    .out_9(decoder_1_out_0[9]), .out_10(decoder_1_out_0[10]), .out_11(decoder_1_out_0[11]),
    .out_12(decoder_1_out_0[12]), .out_13(decoder_1_out_0[13]), .out_14(decoder_1_out_0[14]),
    .out_15(decoder_1_out_0[15]), .out_16(decoder_1_out_0[16]), .out_17(decoder_1_out_0[17]),
    .out_18(decoder_1_out_0[18]), .out_19(decoder_1_out_0[19]), .out_20(decoder_1_out_0[20]),
    .out_21(decoder_1_out_0[21]), .out_22(decoder_1_out_0[22]), .out_23(decoder_1_out_0[23]),
    .out_24(decoder_1_out_0[24]), .out_25(decoder_1_out_0[25]), .out_26(decoder_1_out_0[26]),
    .out_27(decoder_1_out_0[27]), .out_28(decoder_1_out_0[28]), .out_29(decoder_1_out_0[29]),
    .out_30(decoder_1_out_0[30]), .out_31(decoder_1_out_0[31]), .out_32(decoder_1_out_0[32]),
    .out_33(decoder_1_out_0[33]), .out_34(decoder_1_out_0[34]), .out_35(decoder_1_out_0[35]),
    .out_36(decoder_1_out_0[36]), .out_37(decoder_1_out_0[37]), .out_38(decoder_1_out_0[38]),
    .out_39(decoder_1_out_0[39]), .out_40(decoder_1_out_0[40]), .out_41(decoder_1_out_0[41]),
    .out_42(decoder_1_out_0[42]), .out_43(decoder_1_out_0[43]), .out_44(decoder_1_out_0[44]),
    .out_45(decoder_1_out_0[45]), .out_46(decoder_1_out_0[46]), .out_47(decoder_1_out_0[47]),
    .out_48(decoder_1_out_0[48]), .out_49(decoder_1_out_0[49]), .out_50(decoder_1_out_0[50]),
    .out_51(decoder_1_out_0[51]), .out_52(decoder_1_out_0[52]), .out_53(decoder_1_out_0[53]),
    .out_54(decoder_1_out_0[54]), .out_55(decoder_1_out_0[55]), .out_56(decoder_1_out_0[56]),
    .out_57(decoder_1_out_0[57]), .out_58(decoder_1_out_0[58]), .out_59(decoder_1_out_0[59]),
    .out_60(decoder_1_out_0[60]), .out_61(decoder_1_out_0[61]), .out_62(decoder_1_out_0[62]),
    .out_63(decoder_1_out_0[63]));
endmodule

/* Test case:
e en 63 62 61 60 59 58 57 56 55 54 53 52 51 50 49 48 47 46 45 44 43 42 41 40 39 38 37 36 35 34 33 32 

repeat(42)(n+32) 1 bits (32, 1<<(n))
repeat(32)(n+32) 0 bits (32, 0)
*/

/* Test case:
e en 31 30 29 28 27 26 25 24 23 22 21 20 19 18 17 16 15 14 13 12 11 10 9 8 7 6 5 4 3 2 1 0

repeat(32)(n) 1 bits (32, 1<<n)
repeat(32)(n) 0 bits (32, 0)
*/
