// Digital circuit div.dig as structural Verilog
module div (
  input  [31:0] A,
  input  [31:0] B,
  output [31:0] q,
  output [31:0] r
);

  wire comparator_1_lt, comparator_2_eq;
  wire [31:0] add_1_s, add_2_s, multiplexer_1_out, multiplexer_2_out, q1, r1, sub_1_s, sub_2_s;

  Div #(.Signed("true"), .Bits(32)) \div_signé  (.a(A), .b(B), .q(q1), .r(r1));
  Sub #(.Bits(32)) sub_1 (.a(r1), .b(B), .c_i(1'b0), .s(sub_1_s));  // open: c_o
  Add #(.Bits(32)) add_1 (.a(q1), .b(32'h1), .c_i(1'b0), .s(add_1_s));  // open: c_o
  Comparator #(.Signed("true"), .Bits(32)) comparator_1 (.a(q1), .b({32{1'b0}}), .lt(comparator_1_lt));  // open: gt, eq
  Multiplexer #(.Bits(32)) multiplexer_1 (.sel(comparator_1_lt), .in_0(q1), .in_1(add_1_s), .out(multiplexer_1_out));
  Multiplexer #(.Bits(32)) multiplexer_2 (.sel(comparator_1_lt), .in_0(r1), .in_1(sub_1_s), .out(multiplexer_2_out));
  Sub #(.Bits(32)) sub_2 (.a({32{1'b0}}), .b(B), .c_i(1'b0), .s(sub_2_s));  // open: c_o
  Add #(.Bits(32)) add_2 (.a(multiplexer_1_out), .b({32{1'b1}}), .c_i(1'b0), .s(add_2_s));  // open: c_o
  Comparator #(.Signed("true"), .Bits(32)) comparator_2 (
    .a(multiplexer_2_out), .b(sub_2_s), .eq(comparator_2_eq));  // open: gt, lt
  Multiplexer #(.Bits(32)) multiplexer_3 (.sel(comparator_2_eq), .in_0(multiplexer_1_out), .in_1(add_2_s), .out(q));
  Multiplexer #(.Bits(32)) multiplexer_4 (.sel(comparator_2_eq), .in_0(multiplexer_2_out), .in_1({32{1'b0}}), .out(r));
endmodule

/* Test case:
A   B   q   r 
0xFFFFFFF6   3  0xFFFFFFFD   0xFFFFFFFF
*/
