// Digital circuit encodeur32.dig as structural Verilog
module encodeur32 (
  input  _0,
  input  _1,
  input  _2,
  input  _3,
  input  _4,
  input  _5,
  input  _6,
  input  _7,
  input  _8,
  input  _9,
  input  _10,
  input  _11,
  input  _12,
  input  _13,
  input  _14,
  input  _15,
  input  _16,
  input  _17,
  input  _18,
  input  _19,
  input  _20,
  input  _21,
  input  _22,
  input  _23,
  input  _24,
  input  _25,
  input  _26,
  input  _27,
  input  _28,
  input  _29,
  input  _30,
  input  _31,
  output [4:0] s
);

  or or_1 (s[0], _1, _3, _5, _7, _9, _11, _13, _15, _17, _19, _21, _23, _25, _27, _29, _31);
  or or_2 (s[1], _2, _3, _6, _7, _10, _11, _14, _15, _18, _19, _22, _23, _26, _27, _30, _31);
  or or_3 (s[2], _4, _5, _6, _7, _12, _13, _14, _15, _20, _21, _22, _23, _28, _29, _30, _31);
  or or_4 (s[3], _8, _9, _10, _11, _12, _13, _14, _15, _24, _25, _26, _27, _28, _29, _30, _31);
  or or_5 (s[4], _16, _17, _18, _19, _20, _21, _22, _23, _24, _25, _26, _27, _28, _29, _30, _31);

  // Other names for the same wires on the sheet: t0 = _0; t1 = _1; t2 = _2; t3 = _3; t4 = _4; t5 = _5; t6 = _6;
  //   t7 = _7; t8 = _8; t9 = _9; t10 = _10; t11 = _11; t12 = _12; t13 = _13; t14 = _14; t15 = _15; t16 = _16;
  //   t17 = _17; t18 = _18; t19 = _19; t20 = _20; t21 = _21; t22 = _22; t23 = _23; t24 = _24; t25 = _25; t26 = _26;
  //   t27 = _27; t28 = _28; t29 = _29; t30 = _30; t31 = _31
endmodule

/* Test case:
s 31 30 29 28 27 26 25 24 23 22 21 20 19 18 17 16 15 14 13 12 11 10 9 8 7 6 5 4 3 2 1 0

repeat(32)(n) bits (32, 1<<n)
*/
