// Digital circuit mips.dig as structural Verilog
module mips (
  input  [31:0] MiOp,
  input  [31:0] MdD,
  input  C,
  input  [31:0] RegDa,
  input  [31:0] RegDb,
  input  MdVm,
  output [31:0] MiAd,
  output [31:0] MdA,
  output [31:0] MdDin,
  output Mdstr,
  output Mdld,
  output [31:0] RegDin,
  output [4:0] RegRw,
  output [4:0] RegRa,
  output [4:0] RegRb,
  output RegC,
  output Regereg,
  output Md8,
  output [31:0] cps,
  output Mdcns
);

  wire and_1_out, and_2_out, and_3_out, and_4_out, and_5_out, and_6_out, beq, bgez, bgtz, blez, bltz, bne,
       \break , comparator_1_eq, eq_0, jal, jr, lt_0, lt__eq_0, mx_1, mx_br, mx_shamt, Ns;
  wire [4:0] multiplexer_2_out, Op_ual;
  wire [31:0] add_2_s, cp_plus_4, Imms, Imms_lt__lt_2, multiplexer_1_out, multiplexer_3_out,
       multiplexer_5_out, multiplexer_9_out, multiplexer_10_out, multiplexer_11_out, register_1_q;

  Add #(.Bits(32)) add_1 (.a(MiAd), .b(32'h4), .c_i(1'b0), .s(cp_plus_4));  // open: c_o
  Add #(.Bits(32)) add_2 (.a(cp_plus_4), .b(Imms_lt__lt_2), .c_i(1'b0), .s(add_2_s));  // open: c_o
  Multiplexer #(.Bits(32)) multiplexer_1 (.sel(Mdld), .in_0(MdA), .in_1(MdD), .out(multiplexer_1_out));
  Multiplexer #(.Bits(5)) multiplexer_2 (.sel(mx_1), .in_0(MiOp[20:16]), .in_1(MiOp[15:11]), .out(multiplexer_2_out));
  Multiplexer #(.Bits(32)) multiplexer_3 (.sel(mx_br), .in_0(cp_plus_4), .in_1(add_2_s), .out(multiplexer_3_out));
  Multiplexer #(.Bits(5)) multiplexer_4 (.sel(jal), .in_0(multiplexer_2_out), .in_1({5{1'b1}}), .out(RegRw));
  Multiplexer #(.Bits(32)) multiplexer_5 (.sel(jr), .in_0(multiplexer_3_out), .in_1(RegDa), .out(multiplexer_5_out));
  Multiplexer #(.Bits(32)) multiplexer_6 (.sel(jal), .in_0(multiplexer_1_out), .in_1(cp_plus_4), .out(RegDin));
  Delay delay_1 (.in(C), .out(RegC));
  Multiplexer #(.Bits(32)) multiplexer_7 (
    .sel(jal), .in_0(multiplexer_5_out), .in_1({MiAd[31:28], MiOp[25:0], 2'b00}), .out(cps));
  Register #(.Bits(32)) register_1 (.D(cps), .C(~C), .en(1'b1), .Q(register_1_q));
  Comparator #(.Bits(32)) comparator_1 (.a(register_1_q), .b({32{1'b0}}), .eq(comparator_1_eq));  // open: gt, lt
  // Probe on RegDa
  // Probe on RegDb
  Multiplexer #(.Bits(32)) multiplexer_8 (.sel(comparator_1_eq), .in_0(register_1_q), .in_1(32'h400000), .out(MiAd));
  Multiplexer #(.Bits(32)) multiplexer_9 (
    .sel(mx_shamt), .in_0(RegDa), .in_1({{27{1'b0}}, MiOp[10:6]}), .out(multiplexer_9_out));
  Multiplexer #(.Bits(32)) multiplexer_10 (
    .sel(Ns), .in_0(Imms), .in_1({{16{1'b0}}, MiOp[15:0]}), .out(multiplexer_10_out));
  Multiplexer #(.Bits(32)) multiplexer_11 (
    .sel(mx_1), .in_0(multiplexer_10_out), .in_1(RegDb), .out(multiplexer_11_out));
  // Probe on MdA
  ual ual_1 (
    .A(multiplexer_9_out), .B(multiplexer_11_out), .Op(Op_ual), .C(C), .S(MdA), .eq_0(eq_0),
    .lt__eq(lt__eq_0), .lt(lt_0));  // open: HI, LO
  BarrelShifter #(.Bits(32)) barrelshifter_1 (.in(Imms), .shift(6'b000010), .out(Imms_lt__lt_2));
  // Probe break Code on MiOp[25:6]
  BitExtender #(.inputBits(16), .outputBits(32)) bitextender_1 (.in(MiOp[15:0]), .out(Imms));
  and and_1 (and_1_out, bne, ~eq_0);  // And
  and and_2 (and_2_out, beq, eq_0);
  and and_3 (and_3_out, bgtz, ~lt__eq_0);  // And
  and and_4 (and_4_out, blez, lt__eq_0);
  and and_5 (and_5_out, bltz, lt_0);
  and and_6 (and_6_out, bgez, ~lt_0);  // And
  cmd cmd_1 (
    .Co(MiOp[31:26]), .Nf(MiOp[5:0]), .nrt(MiOp[20:16]), .ld(Mdld), .str(Mdstr), .mx1(mx_1), .bne(bne),
    .beq(beq), .blez(blez), .bgtz(bgtz), .jal(jal), .jr(jr), .Ns(Ns), .Op(Op_ual), .ereg(Regereg),
    .shamt(mx_shamt), .M8(Md8), .\break (\break ), .bltz(bltz), .bgez(bgez), .cns(Mdcns));
  or or_1 (mx_br, and_1_out, and_2_out, and_3_out, and_4_out, and_5_out, and_6_out);

  assign MdDin = RegDb;
  assign RegRa = MiOp[25:21];
  assign RegRb = MiOp[20:16];

  // Other names for the same wires on the sheet: cns = Mdcns; data_read[31:0] = MdD; ereg = Regereg; ld = Mdld;
  //   mem_8 = Md8; Imm26[31:2] = {MiAd[31:28], MiOp[25:0]}; ImmNs[15:0] = MiOp[15:0]; Nf[5:0] = MiOp[5:0];
  //   shamt[4:0] = MiOp[10:6]; num_rd[4:0] = MiOp[15:11]; num_rt[4:0] = MiOp[20:16]; num_rs[4:0] = MiOp[25:21];
  //   Co[5:0] = MiOp[31:26]; not_used = MdVm; pour_test[31:0] = cps; RegNumrw[4:0] = RegRw; res_ual[31:0] = MdA;
  //   str = Mdstr; val_rs[31:0] = RegDa; val_rt[31:0] = RegDb

  // Notes on the sheet:
  //   Calcul cp suivant
  //   UAL
  //   Vers/depuis Banc registres
  //   Vers/depuis Mem données
  //   décodage
  //   Commande
  //   Vers/depuis Mem inst
  //   Saut et Branchement
endmodule

/* Test case:
MiOp		C	MdD	RegDa	RegDb	RegDin	RegRw	RegC	RegRa	RegRb	Regereg	MdA	MdDin	Mdstr	Mdld	Md8	Mdcns	cps		MiAd	
0x824020	x	0	4	3	7	8	x	4	2	1	7	3	0	0	0	0	0x400004	0x400000	# add $t0,$a0,$v0
0x2082FFFF	x	0	2	0x99	1	2	x	4	2	1	1	0x99	0	0	0	0	0x400008	0x400004	# addi $v0, $a0,-1
0x000247C3	x	0	0x99	5	0	8	x	0	2	1	0	5	0	0	0	0	0x40000C	0x400008	# sra $t0,$v0,31
0x8C82FFFC	x	7	5	0x99	7	2	x	4	2	1	1	0x99	0	1	0	0	0x400010	0x40000C	# lw $v0,-4($a0)
0x1482FFFE	x	0	5	4	1	31	x	4	2	0	1	4	0	0	0	0	0x40000C	0x400010	# bne $a0,$v0,ici
*/
