// Digital circuit ual.dig as structural Verilog
module ual (
  input  [31:0] A,
  input  [31:0] B,
  input  [4:0] Op,
  input  C,
  output [31:0] S,
  output eq_0,
  output lt__eq,
  output lt,
  output [31:0] HI,
  output [31:0] LO
);

  wire cdiv, cdivu, cmult, cmultu, or_2_out, or_3_out;
  wire [0:0] slt, sltu;
  wire [31:0] add, \and , divH, divL, divuH, divuL, lui, mfhi, mflo, mulH, mulL, multiplexer_1_out,
       multiplexer_2_out, multiplexer_3_out, multiplexer_4_out, multuH, multuL, \nor , \or , sll, sra, srl,
       sub, \xor ;

  Add #(.Bits(32)) u_add (.a(A), .b(B), .c_i(1'b0), .s(add));  // open: c_o
  assign \and  = A & B;  // And and_1, 32 bits wide
  assign \or  = A | B;  // Or or_1, 32 bits wide
  assign \nor  = ~(A | B);  // NOr nor_1, 32 bits wide
  assign \xor  = A ^ B;  // XOr xor_1, 32 bits wide
  BarrelShifter #(.Bits(32)) u_sll (.in(B), .shift({1'b0, A[4:0]}), .out(sll));
  BarrelShifter #(.Bits(32), .direction("right")) u_srl (.in(B), .shift({1'b0, A[4:0]}), .out(srl));
  BarrelShifter #(.barrelShifterMode("arithmetic"), .Bits(32), .direction("right")) u_sra (
    .in(B), .shift({1'b0, A[4:0]}), .out(sra));
  Sub #(.Bits(32)) u_sub (.a(A), .b(B), .c_i(1'b0), .s(sub));  // open: c_o
  BarrelShifter #(.Bits(32)) u_lui (.in(B), .shift(6'b010000), .out(lui));
  Comparator #(.Signed("true"), .Bits(32)) u_slt (.a(A), .b(B), .lt(slt[0]));  // open: gt, eq
  Comparator #(.Bits(32)) u_sltu (.a(A), .b(B), .lt(sltu[0]));  // open: gt, eq
  Mul #(.Signed("true"), .Bits(32)) mult (.a(A), .b(B), .mul({mulH, mulL}));
  Mul #(.Bits(32)) multu (.a(A), .b(B), .mul({multuH, multuL}));
  div div_1 (.A(A), .B(B), .q(divL), .r(divH));
  Div #(.Bits(32)) divu (.a(A), .b(B), .q(divuL), .r(divuH));
  Decoder #(.Selector_Bits(5)) decoder_1 (
    .sel(Op), .out_15(cmult), .out_16(cmultu), .out_17(cdiv), .out_18(cdivu));  // open: out_0, out_1, out_2, out_3, out_4, out_5, out_6, out_7, out_8, out_9, out_10, out_11, out_12, out_13, out_14, out_19, out_20, out_21, out_22, out_23, out_24, out_25, out_26, out_27, out_28, out_29, out_30, out_31
  Multiplexer #(.Bits(32)) multiplexer_1 (.sel(cmultu), .in_0(mulH), .in_1(multuH), .out(multiplexer_1_out));
  Multiplexer #(.Bits(32)) multiplexer_2 (.sel(cmultu), .in_0(mulL), .in_1(multuL), .out(multiplexer_2_out));
  Multiplexer #(.Bits(32)) multiplexer_3 (.sel(cdiv), .in_0(multiplexer_1_out), .in_1(divH), .out(multiplexer_3_out));
  Multiplexer #(.Bits(32)) multiplexer_4 (.sel(cdiv), .in_0(multiplexer_2_out), .in_1(divL), .out(multiplexer_4_out));
  or or_2 (or_2_out, cmult, cmultu, cdiv, cdivu);
  or or_3 (or_3_out, cmult, cmultu, cdiv, cdivu);
  Multiplexer #(.Bits(32)) multiplexer_5 (.sel(cdivu), .in_0(multiplexer_3_out), .in_1(divuH), .out(HI));
  Multiplexer #(.Bits(32)) multiplexer_6 (.sel(cdivu), .in_0(multiplexer_4_out), .in_1(divuL), .out(LO));
  Register #(.Bits(32)) u_HI (.D(HI), .C(C), .en(or_2_out), .Q(mfhi));
  Register #(.Bits(32)) u_LO (.D(LO), .C(C), .en(or_3_out), .Q(mflo));
  Comparator #(.Signed("true"), .Bits(32)) comparator_1 (.a(S), .b({32{1'b0}}), .eq(eq_0), .lt(lt));  // open: gt
  or or_4 (lt__eq, eq_0, lt);
  Multiplexer #(.Selector_Bits(4), .Bits(32)) multiplexer_7 (
    .sel(Op[3:0]), .in_0(add), .in_1(\and ), .in_2(\or ), .in_3(\nor ), .in_4(\xor ), .in_5(sll), .in_6(srl),
    .in_7(sra), .in_8(sub), .in_9(lui), .in_10(mfhi), .in_11(mflo), .in_12({{31{1'b0}}, slt[0]}),
    .in_13({{31{1'b0}}, sltu[0]}), .in_14(A), .in_15({32{1'b0}}), .out(S));

  // Other names for the same wires on the sheet: dec[4:0] = A[4:0]; out[31:0] = S

  // Notes on the sheet:
  //   Calcul résultat
  //   HI / LO
  //   Input / Output
endmodule

/* Test case:
Op	A	B	S	=0	<	<=	LO	HI	# 
0	5	(-11)	(-6)	0	1	1	x	x 	# add
0	10	(-4)	6	0	0	0	x	x	# add
1	1	2	0	1	0	1	x	x	# and
2	1	2	3	0	0	0	x	x	# or
3	1	2	(-4)	0	1	1	x	x	# nor
4	1	2	3	0	0	0	x	x	# xor
5	1	3	6	0	0	0	x	x	# sll
6	1	3	1	0	0	0	x	x	# srl
7	1	(-2)	(-1)	0	1	1	x	x	# sra
8	1	3	(-2)	0	1	1	x	x	# sub
9	x	0xA	0xA0000	0	0	0	x	x	# lui
10	x	x	0	1	0	1	x	x	# mfhi
11	x	x	0	1	0	1	x	x	# mflo
12	(-1)	4	1	0	0	0	x	x	# slt
12	4	(-1)	0	1	0	1	x	x	# slt
13	(-1)	4	0	1	0	1	x	x	# sltu
13	4	(-1)	1	0	0	0	x	x	# sltu
14	5	x	5	0	0	0	x	x	# lire A
15	(-2)	(-3)	x	x	x	x	6	0	# mult
15	(-2)	3	x	x	x	x	(-6)	(-1)	# mult
16	(-2)	2	x	x	x	x	(-4)	1 	# multu
17	(-11)	3	x	x	x	x	(-3)	(-2)	# div
18	(-1)	2	x	x	x	x	0x7FFFFFFF 1	# divu
*/
